# Fritzing sketch sketch paindre (saved by Fritzing 0.9.2b)

parts:
  U1 = ESP32-38PinWide [part_number=ESP32-38PinWide]
  IR1 = TSOP312.., 314.. [package=THT]
  LED1 = LED - 3mm [color="Green (570nm)" package="3 mm [THT]"]
  part = TTP223B Capacitive Touch Sensor Module [part_number="Touch sensor"]
  R1 = Resistor [tolerance=±5% resistance=220 package="2512 [SMD]"]
  J1 = Basic Servo

nets:
  N1: U1.3.3, IR1.Vs, part.VCC
  GND: U1.GND, IR1.GND, part.GND, R1.Pin_0, J1.gnd
  VIN: U1.VIN, J1.vcc
  N2: U1.GPIO16, LED1.cathode
  N3: U1.GPIO17, part.SIG
  N4: U1.GPIO5, J1.pulse
  N5: U1.GPIO22, IR1.Data

custom parts:
  ESP32-38PinWide: Generic 38-Pin ESP32 with wide format (only access to one side of pins on a breadboard) based on Stephen Lilley's HiLetgo ESP-WROOM-32 ESP32 ESP-32S Development Board.
  TTP223B Capacitive Touch Sensor Module: The TTP223B capacitive touch sensor module uses the TTP223B IC. The appropriate voltage is approximately 2 to 5.5 volts.
